// Logisim project Brenda_Aguiar_Multiplicador_8bits(1).circ as structural Verilog: 6 circuits, main circuit 1 bit half adder
module _1_bit_half_adder (
  input  A,
  input  B,
  output C_OUT,
  output R
);

  and and_1 (C_OUT, A, B);
  XOR xor_1 (.in_1(A), .in_2(B), .out_3(R));
endmodule

module XOR (
  input  in_1,
  input  in_2,
  output out_3
);

  wire and_1_out, and_2_out, not_1_out, not_2_out;

  not not_1 (not_1_out, in_2);
  not not_2 (not_2_out, in_1);
  and and_1 (and_1_out, in_1, not_1_out);
  and and_2 (and_2_out, not_2_out, in_2);
  or or_1 (out_3, and_1_out, and_2_out);
endmodule

module XNOR (
  input  in_1,
  input  in_2,
  output out_3
);

  wire xor_1_out_3;

  XOR xor_1 (.in_1(in_1), .in_2(in_2), .out_3(xor_1_out_3));
  not not_1 (out_3, xor_1_out_3);
endmodule

module _1_bit_full_adder (
  input  A,
  input  B,
  input  C_IN,
  output C_OUT,
  output R
);

  wire and_1_out, and_2_out, and_3_out, xor_1_out_3;

  XOR xor_1 (.in_1(A), .in_2(B), .out_3(xor_1_out_3));
  and and_1 (and_1_out, A, B);
  and and_2 (and_2_out, A, C_IN);
  and and_3 (and_3_out, B, C_IN);
  XOR xor_2 (.in_1(xor_1_out_3), .in_2(C_IN), .out_3(R));
  or or_1 (C_OUT, and_1_out, and_2_out, and_3_out);
endmodule

module _8_bit_adder (
  input  [7:0] A,
  input  [7:0] B,
  output [7:0] out_3,
  output C_OUT
);

  wire n1_bit_full_adder_1_c_out, n1_bit_full_adder_2_c_out, n1_bit_full_adder_3_c_out,
       n1_bit_full_adder_4_c_out, n1_bit_full_adder_5_c_out, n1_bit_full_adder_6_c_out,
       n1_bit_full_adder_7_c_out;

  _1_bit_full_adder u_1_bit_full_adder_1 (
    .A(A[0]), .B(B[0]), .C_IN(1'b0), .C_OUT(n1_bit_full_adder_1_c_out), .R(out_3[0]));
  _1_bit_full_adder u_1_bit_full_adder_2 (
    .A(A[1]), .B(B[1]), .C_IN(n1_bit_full_adder_1_c_out), .C_OUT(n1_bit_full_adder_2_c_out), .R(out_3[1]));
  _1_bit_full_adder u_1_bit_full_adder_3 (
    .A(A[2]), .B(B[2]), .C_IN(n1_bit_full_adder_2_c_out), .C_OUT(n1_bit_full_adder_3_c_out), .R(out_3[2]));
  _1_bit_full_adder u_1_bit_full_adder_4 (
    .A(A[3]), .B(B[3]), .C_IN(n1_bit_full_adder_3_c_out), .C_OUT(n1_bit_full_adder_4_c_out), .R(out_3[3]));
  _1_bit_full_adder u_1_bit_full_adder_5 (
    .A(A[4]), .B(B[4]), .C_IN(n1_bit_full_adder_4_c_out), .C_OUT(n1_bit_full_adder_5_c_out), .R(out_3[4]));
  _1_bit_full_adder u_1_bit_full_adder_6 (
    .A(A[5]), .B(B[5]), .C_IN(n1_bit_full_adder_5_c_out), .C_OUT(n1_bit_full_adder_6_c_out), .R(out_3[5]));
  _1_bit_full_adder u_1_bit_full_adder_7 (
    .A(A[6]), .B(B[6]), .C_IN(n1_bit_full_adder_6_c_out), .C_OUT(n1_bit_full_adder_7_c_out), .R(out_3[6]));
  _1_bit_full_adder u_1_bit_full_adder_8 (
    .A(A[7]), .B(B[7]), .C_IN(n1_bit_full_adder_7_c_out), .C_OUT(C_OUT), .R(out_3[7]));
endmodule

module \Multiplicação_8_bits  (
  input  [7:0] M,
  input  [2:0] in_2,
  input  [7:0] Q,
  input  Reset,
  output out_5,
  output [7:0] out_6,
  output [7:0] Contador,
  output [15:0] out_8,
  output [7:0] out_9,
  output [7:0] out_10,
  output CARRY_OUT,
  output [15:0] Resultado_de_A_e_Q
);

  wire Clock_out, comparator_1_lt, comparator_2_gt;
  wire [7:0] multiplexer_1_out, register_1_q, register_2_q;
  wire [16:0] shifter_1_out;

  Counter counter_1 (
    .load(1'b0), .count(comparator_2_gt), .Q(Contador), .clk(Clock_out), .clr(Reset));  // open: D, carry
  Clock Clock (.out(Clock_out));
  Multiplexer #(.width(8), .enable("false")) multiplexer_1 (
    .in0(Q), .in1(out_8[7:0]), .out(multiplexer_1_out), .sel(comparator_1_lt));
  Comparator #(.mode("unsigned")) comparator_1 (.a({8{1'b0}}), .b(Contador), .lt(comparator_1_lt));  // open: gt, eq
  Comparator #(.mode("unsigned")) comparator_2 (.a(8'h9), .b(Contador), .gt(comparator_2_gt));  // open: eq, lt
  Register register_1 (.D(multiplexer_1_out), .en(comparator_2_gt), .Q(register_1_q), .clk(Clock_out), .clr(Reset));
  Register register_2 (.D(M), .Q(register_2_q), .clk(Clock_out), .clr(Reset));  // open: en
  Register register_3 (.D(out_8[15:8]), .en(comparator_2_gt), .Q(out_10), .clk(Clock_out), .clr(Reset));
  BitSelector bitselector_1 (.in(register_1_q), .out(out_5), .sel(in_2));
  _8_bit_adder u_8_bit_adder_1 (.A(register_2_q), .B(out_10), .out_3(out_9), .C_OUT(CARRY_OUT));
  Shifter #(.width(17), .shift("lr")) shifter_1 (
    .in({CARRY_OUT, out_6, register_1_q}), .\dist (5'b00001), .out(shifter_1_out));
  Multiplexer #(.width(8)) multiplexer_2 (.in0(out_10), .in1(out_9), .out(out_6), .sel(out_5));  // open: en
  Bit_Extender #(.in_width(17)) bit_extender_1 (.in(shifter_1_out), .out(out_8));
  Bit_Extender #(.in_width(17)) bit_extender_2 (.in({CARRY_OUT, out_6, register_1_q}), .out(Resultado_de_A_e_Q));
endmodule
